// Logisim project ex4.circ as structural Verilog: 4 circuits, main circuit FSM
module FSM (
  input  INPUT0,
  output OUTPUT0
);

  wire clock_1_out;
  wire [1:0] fsmlogic_1_next_state, register_1_q;

  FSMLogic fsmlogic_1 (
    .INPUT0(INPUT0), .CURRENT_STATE(register_1_q), .OUTPUT0(OUTPUT0), .NEXT_STATE(fsmlogic_1_next_state));
  Register #(.width(2)) register_1 (.D(fsmlogic_1_next_state), .clk(clock_1_out), .Q(register_1_q));  // open: en, clr
  Clock clock_1 (.out(clock_1_out));
endmodule

module FSMLogic (
  input  INPUT0,
  input  [1:0] CURRENT_STATE,
  output OUTPUT0,
  output [1:0] NEXT_STATE
);

  wire and_1_out, and_2_out, not_1_out, not_2_out, not_3_out;

  not not_1 (not_1_out, INPUT0);
  not not_2 (not_2_out, CURRENT_STATE[0]);
  not not_3 (not_3_out, CURRENT_STATE[1]);
  and and_1 (and_1_out, not_1_out, not_2_out);
  and and_2 (and_2_out, INPUT0, not_3_out);
  StateBit0 statebit0_1 (.INPUT0(INPUT0), .CURRENT_STATE(CURRENT_STATE), .NEW_STATE_BIT_0(NEXT_STATE[0]));
  StateBit1 statebit1_1 (.INPUT0(INPUT0), .CURRENT_STATE(CURRENT_STATE), .NEW_STATE_BIT_1(NEXT_STATE[1]));
  or or_1 (OUTPUT0, and_1_out, and_2_out);

  // Other names for the same wires on the sheet: CurrentState[1:0] = CURRENT_STATE;
  //   CurrentStateBit0 = CURRENT_STATE[0]; CurrentStateBit1 = CURRENT_STATE[1]
endmodule

module StateBit0 (
  input  INPUT0,
  input  [1:0] CURRENT_STATE,
  output NEW_STATE_BIT_0
);

  wire and_1_out, INPUT_0, L0, nor_1_out, or_2_out, R0;

  not not_1 (INPUT_0, INPUT0);
  not not_2 (R0, CURRENT_STATE[0]);
  not not_3 (L0, CURRENT_STATE[1]);
  and and_1 (and_1_out, CURRENT_STATE[1], INPUT0);
  nor nor_1 (nor_1_out, L0, INPUT0);
  or or_1 (NEW_STATE_BIT_0, INPUT_0, or_2_out);
  or or_2 (or_2_out, and_1_out, nor_1_out);

  // Other names for the same wires on the sheet: R1 = CURRENT_STATE[0]; L1 = CURRENT_STATE[1]; INPUT_1 = INPUT0
endmodule

module StateBit1 (
  input  INPUT0,
  input  [1:0] CURRENT_STATE,
  output NEW_STATE_BIT_1
);

  wire and_1_out, INPUT_0, L0, nor_1_out, or_2_out, R0;

  not not_1 (INPUT_0, INPUT0);
  not not_2 (R0, CURRENT_STATE[0]);
  not not_3 (L0, CURRENT_STATE[1]);
  or or_1 (NEW_STATE_BIT_1, INPUT0, or_2_out);
  nor nor_1 (nor_1_out, R0, INPUT_0);
  and and_1 (and_1_out, INPUT_0, CURRENT_STATE[0]);
  or or_2 (or_2_out, nor_1_out, and_1_out);

  // Other names for the same wires on the sheet: R1 = CURRENT_STATE[0]; L1 = CURRENT_STATE[1]; INPUT_1 = INPUT0
endmodule
