// Logisim project ex6.circ as structural Verilog: 5 circuits, main circuit RotRight
module RotRight (
  input  [15:0] INPUT0,
  input  [3:0] AMOUNT,
  output [15:0] OUTPUT0
);

  wire [15:0] and_1_out, and_2_out, and_3_out, and_4_out, and_5_out, and_6_out, and_7_out, and_8_out,
       bit_extender_1_out, bit_extender_2_out, bit_extender_3_out, bit_extender_4_out, not_1_out, not_2_out,
       not_3_out, not_4_out, or_1_out, or_2_out, or_3_out, rot1_1_out_2, rot2_1_out_2, rot4_1_out_2,
       rot8_1_out_2;

  assign bit_extender_1_out = {{15{AMOUNT[0]}}, AMOUNT[0]};  // Bit_Extender bit_extender_1
  assign bit_extender_2_out = {{15{AMOUNT[2]}}, AMOUNT[2]};  // Bit_Extender bit_extender_2
  assign bit_extender_3_out = {{15{AMOUNT[3]}}, AMOUNT[3]};  // Bit_Extender bit_extender_3
  assign not_1_out = ~bit_extender_1_out;  // NOT_Gate not_1, 16 bits wide
  assign and_1_out = INPUT0 & bit_extender_1_out;  // AND_Gate and_1, 16 bits wide
  assign bit_extender_4_out = {{15{AMOUNT[1]}}, AMOUNT[1]};  // Bit_Extender bit_extender_4
  assign not_2_out = ~bit_extender_2_out;  // NOT_Gate not_2, 16 bits wide
  assign and_2_out = not_2_out & or_3_out;  // AND_Gate and_2, 16 bits wide
  assign and_3_out = bit_extender_2_out & or_3_out;  // AND_Gate and_3, 16 bits wide
  assign and_4_out = bit_extender_3_out & or_2_out;  // AND_Gate and_4, 16 bits wide
  assign and_5_out = INPUT0 & not_1_out;  // AND_Gate and_5, 16 bits wide
  rot1 rot1_1 (.out_2(rot1_1_out_2), .in_1(and_1_out));
  rot4 rot4_1 (.out_2(rot4_1_out_2), .in_1(and_3_out));
  rot8 rot8_1 (.out_2(rot8_1_out_2), .in_1(and_4_out));
  assign or_1_out = and_5_out | rot1_1_out_2;  // OR_Gate or_1, 16 bits wide
  assign not_3_out = ~bit_extender_4_out;  // NOT_Gate not_3, 16 bits wide
  assign and_6_out = or_1_out & bit_extender_4_out;  // AND_Gate and_6, 16 bits wide
  assign or_2_out = and_2_out | rot4_1_out_2;  // OR_Gate or_2, 16 bits wide
  assign not_4_out = ~bit_extender_3_out;  // NOT_Gate not_4, 16 bits wide
  assign and_7_out = not_3_out & or_1_out;  // AND_Gate and_7, 16 bits wide
  assign or_3_out = and_7_out | rot2_1_out_2;  // OR_Gate or_3, 16 bits wide
  rot2 rot2_1 (.out_2(rot2_1_out_2), .in_1(and_6_out));
  assign OUTPUT0 = rot8_1_out_2 | and_8_out;  // OR_Gate or_4, 16 bits wide
  assign and_8_out = not_4_out & or_2_out;  // AND_Gate and_8, 16 bits wide
endmodule

module rot1 (
  input  [15:0] in_1,
  output [15:0] out_2
);

  wire undriven;

  Multiplexer #(.select(4)) multiplexer_1 (
    .in0(in_1[0]), .in1(in_1[1]), .in2(in_1[2]), .in3(in_1[3]), .in4(in_1[4]), .in5(in_1[5]), .in6(in_1[6]),
    .in7(in_1[7]), .in8(in_1[8]), .in9(in_1[9]), .in10(in_1[10]), .in11(in_1[11]), .in12(in_1[12]),
    .in13(in_1[13]), .in14(in_1[14]), .in15(in_1[15]), .out(out_2[15]), .sel(4'b0000), .en(undriven));

  assign out_2[14:0] = in_1[15:1];
endmodule

module rot2 (
  input  [15:0] in_1,
  output [15:0] out_2
);

  wire [15:0] rot1_1_out_2;

  rot1 rot1_1 (.out_2(rot1_1_out_2), .in_1(in_1));
  rot1 rot1_2 (.out_2(out_2), .in_1(rot1_1_out_2));
endmodule

module rot4 (
  input  [15:0] in_1,
  output [15:0] out_2
);

  wire [15:0] rot2_1_out_2;

  rot2 rot2_1 (.out_2(rot2_1_out_2), .in_1(in_1));
  rot2 rot2_2 (.out_2(out_2), .in_1(rot2_1_out_2));
endmodule

module rot8 (
  input  [15:0] in_1,
  output [15:0] out_2
);

  wire [15:0] rot4_1_out_2;

  rot4 rot4_1 (.out_2(rot4_1_out_2), .in_1(in_1));
  rot4 rot4_2 (.out_2(out_2), .in_1(rot4_1_out_2));
endmodule
