// Logisim project alu.circ as structural Verilog: 1 circuit, main circuit alu
module alu (
  input  [31:0] A,
  input  [31:0] B,
  input  [3:0] ALUSel,
  output [31:0] Result
);

  wire comparator_1_lt;
  wire [4:0] bit_extender_1_out, bit_extender_2_out, bit_extender_3_out;
  wire [31:0] ADD0, AND0, MUL0, MULH0, MULHU0, OR0, SLL0, SLT0, SRA0, SRL0, SUB0, XOR0;

  Multiplexer #(.enable("false"), .select(4), .width(32)) multiplexer_1 (
    .in0(ADD0), .in1(SLL0), .in2(SLT0), .in4(XOR0), .in5(SRL0), .in6(OR0), .in7(AND0), .in8(MUL0),
    .in9(MULH0), .in11(MULHU0), .in12(SUB0), .in13(SRA0), .in15(B), .out(Result), .sel(ALUSel));  // open: in3, in10, in14
  Adder #(.width(32)) adder_1 (.a(A), .b(B), .out(ADD0));  // open: cin, cout
  assign XOR0 = A ^ B;  // XOR_Gate xor_1, 32 bits wide
  assign AND0 = A & B;  // AND_Gate and_1, 32 bits wide
  Subtractor #(.width(32)) subtractor_1 (.a(A), .b(B), .out(SUB0));  // open: bin, bout
  Bit_Extender #(.in_width(32), .out_width(5)) bit_extender_1 (.in(B), .out(bit_extender_1_out));
  Bit_Extender #(.in_width(32), .out_width(5)) bit_extender_2 (.in(B), .out(bit_extender_2_out));
  Bit_Extender #(.in_width(32), .out_width(5)) bit_extender_3 (.in(B), .out(bit_extender_3_out));
  Shifter #(.width(32)) shifter_1 (.in(A), .\dist (bit_extender_1_out), .out(SLL0));
  Shifter #(.shift("lr"), .width(32)) shifter_2 (.in(A), .\dist (bit_extender_2_out), .out(SRL0));
  Multiplier #(.mode("twosComplement"), .width(32)) multiplier_1 (.a(A), .b(B), .out(MUL0), .cout(MULH0));  // open: cin
  Shifter #(.shift("ar"), .width(32)) shifter_3 (.in(A), .\dist (bit_extender_3_out), .out(SRA0));
  Comparator #(.width(32)) comparator_1 (.a(A), .b(B), .lt(comparator_1_lt));  // open: gt, eq
  assign SLT0 = {{31{1'b0}}, comparator_1_lt};  // Bit_Extender bit_extender_4
  assign OR0 = A | B;  // OR_Gate or_1, 32 bits wide
  Multiplier #(.width(32)) multiplier_2 (.a(A), .b(B), .cout(MULHU0));  // open: out, cin

  // Notes on the sheet:
  //   INPUTS to your circuit
  //   DON'T CHANGE THE LOCATIONS OF THE INPUTS AND OUTPUTS!
  //   OUTPUT from your circuit
endmodule
