// Logisim project control-logic.circ as structural Verilog: 1 circuit, main circuit control_logic
module control_logic (
  input  [31:0] inst,
  input  BrEq,
  input  BrLt,
  output PCSel,
  output RegWEn,
  output [2:0] ImmSel,
  output BrUn,
  output ASel,
  output BSel,
  output [3:0] ALUSel,
  output MemRW,
  output [1:0] WBSel,
  output CSRSel,
  output CSRWen
);

  wire bit_extender_11_out, undriven;
  wire [3:0] bit_extender_1_out, bit_extender_2_out, bit_extender_3_out, bit_extender_4_out,
       bit_extender_5_out, bit_extender_6_out, bit_extender_7_out, bit_extender_8_out, bit_extender_9_out,
       bit_extender_10_out, opcode_type;
  wire [6:0] and_1_out, and_2_out, and_3_out, and_4_out, and_5_out, and_6_out, and_7_out, and_8_out,
       and_9_out, and_10_out;

  Multiplexer #(.enable("false"), .select(4)) multiplexer_1 (
    .in0(1'b0), .in1(1'b0), .in2(1'b0), .in3(1'b0), .in4(undriven), .in5(1'b0), .in6(1'b0), .in7(1'b1),
    .in8(1'b1), .in9(1'b1), .in10(1'b1), .out(PCSel), .sel(opcode_type));  // open: in11, in12, in13, in14, in15
  Multiplexer #(.enable("false"), .select(4)) multiplexer_2 (
    .in0(1'b0), .in1(1'b0), .in2(1'b0), .in3(1'b0), .in4(1'b1), .in5(1'b1), .in6(1'b0), .in7(1'b1),
    .in8(1'b1), .in9(1'b0), .out(ASel), .sel(opcode_type));  // open: in10, in11, in12, in13, in14, in15
  Multiplexer #(.enable("false"), .select(4)) multiplexer_3 (
    .in0(1'b1), .in1(1'b1), .in2(1'b1), .in3(1'b1), .in4(1'b0), .in5(1'b0), .in6(1'b1), .in7(1'b1),
    .in8(1'b1), .in9(1'b1), .in10(1'b0), .out(RegWEn), .sel(opcode_type));  // open: in11, in12, in13, in14, in15
  Multiplexer #(.enable("false"), .select(4), .width(3)) multiplexer_4 (
    .in2(3'b000), .in7(3'b100), .in8(3'b000), .in9(3'b000), .out(ImmSel), .sel(opcode_type));  // open: in0, in1, in3, in4, in5, in6, in10, in11, in12, in13, in14, in15
  assign and_1_out = inst[6:0] & 7'b0110011;  // AND_Gate and_1, 7 bits wide
  assign and_2_out = inst[6:0] & 7'b0000011;  // AND_Gate and_2, 7 bits wide
  assign and_3_out = inst[6:0] & 7'b0010011;  // AND_Gate and_3, 7 bits wide
  assign and_4_out = inst[6:0] & 7'b0100011;  // AND_Gate and_4, 7 bits wide
  assign and_5_out = inst[6:0] & 7'b1100011;  // AND_Gate and_5, 7 bits wide
  assign and_6_out = inst[6:0] & 7'b0010111;  // AND_Gate and_6, 7 bits wide
  assign and_7_out = inst[6:0] & 7'b0110111;  // AND_Gate and_7, 7 bits wide
  assign and_8_out = inst[6:0] & 7'b1101111;  // AND_Gate and_8, 7 bits wide
  assign and_9_out = inst[6:0] & 7'b1100111;  // AND_Gate and_9, 7 bits wide
  assign and_10_out = inst[6:0] & 7'b1110011;  // AND_Gate and_10, 7 bits wide
  Bit_Extender #(.in_width(7), .out_width(4)) bit_extender_1 (.in(and_1_out), .out(bit_extender_1_out));
  Bit_Extender #(.in_width(7), .out_width(4)) bit_extender_2 (.in(and_2_out), .out(bit_extender_2_out));
  Bit_Extender #(.in_width(7), .out_width(4)) bit_extender_3 (.in(and_3_out), .out(bit_extender_3_out));
  Bit_Extender #(.in_width(7), .out_width(4)) bit_extender_4 (.in(and_4_out), .out(bit_extender_4_out));
  Bit_Extender #(.in_width(7), .out_width(4)) bit_extender_5 (.in(and_5_out), .out(bit_extender_5_out));
  Bit_Extender #(.in_width(7), .out_width(4)) bit_extender_6 (.in(and_6_out), .out(bit_extender_6_out));
  Bit_Extender #(.in_width(7), .out_width(4)) bit_extender_7 (.in(and_7_out), .out(bit_extender_7_out));
  Bit_Extender #(.in_width(7), .out_width(4)) bit_extender_8 (.in(and_8_out), .out(bit_extender_8_out));
  Bit_Extender #(.in_width(7), .out_width(4)) bit_extender_9 (.in(and_9_out), .out(bit_extender_9_out));
  Bit_Extender #(.in_width(7), .out_width(4)) bit_extender_10 (.in(and_10_out), .out(bit_extender_10_out));
  assign opcode_type = 4'b0000 & bit_extender_1_out;  // AND_Gate and_11, 4 bits wide
  assign opcode_type = 4'b0001 & bit_extender_2_out;  // AND_Gate and_12, 4 bits wide
  assign opcode_type = 4'b0010 & bit_extender_3_out;  // AND_Gate and_13, 4 bits wide
  assign opcode_type = 4'b0011 & bit_extender_4_out;  // AND_Gate and_14, 4 bits wide
  assign opcode_type = 4'b0100 & bit_extender_5_out;  // AND_Gate and_15, 4 bits wide
  assign opcode_type = 4'b0101 & bit_extender_6_out;  // AND_Gate and_16, 4 bits wide
  assign opcode_type = 4'b0110 & bit_extender_7_out;  // AND_Gate and_17, 4 bits wide
  assign opcode_type = 4'b0111 & bit_extender_8_out;  // AND_Gate and_18, 4 bits wide
  assign opcode_type = 4'b1000 & bit_extender_9_out;  // AND_Gate and_19, 4 bits wide
  assign opcode_type = 4'b1001 & bit_extender_10_out;  // AND_Gate and_20, 4 bits wide
  Bit_Extender #(.in_width(4), .out_width(1)) bit_extender_11 (.in(opcode_type), .out(bit_extender_11_out));
  Multiplexer #(.select(3)) multiplexer_5 (
    .in0(1'b0), .in1(1'b1), .in4(1'b1), .in5(1'b0), .in6(1'b1), .in7(1'b0), .out(BrUn), .sel(inst[14:12]),
    .en(bit_extender_11_out));  // open: in2, in3

  // Other names for the same wires on the sheet: opcode[6:0] = inst[6:0]; funct3[2:0] = inst[14:12];
  //   funct7[6:0] = inst[31:25]

  // Notes on the sheet:
  //   INPUTS to your circuit
  //   DON'T CHANGE THE LOCATIONS OF THE INPUTS AND OUTPUTS!
  //   OUTPUT from your circuit
endmodule
