// Logisim project cpu.circ as structural Verilog: 1 circuit, main circuit cpu
module cpu (
  input  clk,
  input  [31:0] INSTRUCTION,
  input  [31:0] READ_DATA,
  output [31:0] WRITE_ADDRESS,
  output [31:0] PROGRAM_COUNTER,
  output [31:0] ra,
  output [31:0] sp,
  output [31:0] t0,
  output [31:0] t1,
  output [31:0] t2,
  output [31:0] s0,
  output [31:0] s1,
  output [31:0] a0,
  output [31:0] tohost,
  output [3:0] WRITE_ENABLE,
  output [31:0] WRITE_DATA
);

  wire branch_comp_1_p1, branch_comp_1_p2, control_logic_1_asel, control_logic_1_brun, control_logic_1_bsel,
       control_logic_1_csrsel, control_logic_1_csrwen, control_logic_1_memrw, control_logic_1_regwen, PCSel;
  wire [1:0] control_logic_1_wbsel;
  wire [2:0] control_logic_1_immsel;
  wire [3:0] control_logic_1_alusel;
  wire [31:0] imm_gen_1_p3, imm_gen_1_p4, multiplexer_2_out, multiplexer_3_out, multiplexer_4_out,
       multiplexer_5_out, PC4;

  Adder #(.width(32)) adder_1 (.a(PROGRAM_COUNTER), .b(32'h4), .out(PC4));  // open: cin, cout
  Register #(.width(32)) PC (.D(PC4), .clk(clk), .Q(PROGRAM_COUNTER));  // open: en, clr
  Multiplexer #(.enable("false"), .width(32)) multiplexer_1 (.in0(PC4), .in1(WRITE_ADDRESS));  // open: out, sel
  control_logic control_logic_1 (
    .CSRWen(control_logic_1_csrwen), .PCSel(PCSel), .RegWEn(control_logic_1_regwen),
    .ImmSel(control_logic_1_immsel), .BrUn(control_logic_1_brun), .ASel(control_logic_1_asel),
    .BSel(control_logic_1_bsel), .ALUSel(control_logic_1_alusel), .MemRW(control_logic_1_memrw),
    .WBSel(control_logic_1_wbsel), .CSRSel(control_logic_1_csrsel), .inst(INSTRUCTION),
    .BrEq(branch_comp_1_p1), .BrLt(branch_comp_1_p2));
  // imm_gen imm_gen_1: pin names not known; wires that end beside it: INSTRUCTION, control_logic_1_immsel, imm_gen_1_p3, imm_gen_1_p4, WRITE_DATA, control_logic_1_brun
  regfile regfile_1 (
    .rs1(INSTRUCTION[19:15]), .rs2(INSTRUCTION[24:20]), .rd(INSTRUCTION[11:7]),
    .Write_Data(multiplexer_5_out), .RegWEn(control_logic_1_regwen), .clk(clk), .ra(ra), .sp(sp), .t0(t0),
    .t1(t1), .t2(t2), .s0(s0), .s1(s1), .a0(a0), .Read_Data_1(imm_gen_1_p4), .Read_Data_2(WRITE_DATA));
  // branch_comp branch_comp_1: pin names not known; wires that end beside it: branch_comp_1_p1, branch_comp_1_p2
  assign WRITE_ENABLE = {{3{control_logic_1_memrw}}, control_logic_1_memrw};  // Bit_Extender bit_extender_1
  Multiplexer #(.enable("false"), .width(32)) multiplexer_2 (
    .in0(WRITE_DATA), .in1(imm_gen_1_p3), .out(multiplexer_2_out), .sel(control_logic_1_bsel));
  Multiplexer #(.enable("false"), .width(32)) multiplexer_3 (
    .in0(PROGRAM_COUNTER), .in1(imm_gen_1_p4), .out(multiplexer_3_out), .sel(control_logic_1_asel));
  // alu alu_1: pin names not known; wires that end beside it: multiplexer_3_out, multiplexer_2_out, control_logic_1_alusel, WRITE_ADDRESS
  Multiplexer #(.enable("false"), .width(32)) multiplexer_4 (
    .in0(imm_gen_1_p4), .in1(imm_gen_1_p3), .out(multiplexer_4_out), .sel(control_logic_1_csrsel));
  csr csr_1 (
    .CSR_address(INSTRUCTION[31:20]), .CSR_din(multiplexer_4_out), .CSR_WE(control_logic_1_csrwen),
    .clk(clk), .tohost(tohost));
  Multiplexer #(.enable("false"), .select(2), .width(32)) multiplexer_5 (
    .in0(PC4), .in1(WRITE_ADDRESS), .in2(READ_DATA), .out(multiplexer_5_out), .sel(control_logic_1_wbsel));  // open: in3

  // Other names for the same wires on the sheet: ALU_OUTPUT[31:0] = WRITE_ADDRESS

  // Notes on the sheet:
  //   Output to IMEM
  //   IMEM (do **NOT** move this)
  //   Inputs from IMEM
  //   It is OK to move the PC, RegFile, ALU, MEM, Branch Comp, Imm Gen, and Control Logic to wherever is most convenient for you when constructing your CPU, and to delete this text
  //   Inputs/Outputs for testing. Do **NOT** move these.
  //   Outputs To DMEM
  //   DMEM (do **NOT** move this)
  //   Inputs From DMEM
endmodule
