// Logisim project regfile.circ as structural Verilog: 1 circuit, main circuit regfile
module regfile (
  input  [4:0] rs1,
  input  [4:0] rs2,
  input  [4:0] rd,
  input  [31:0] Write_Data,
  input  RegWEn,
  input  clk,
  output [31:0] ra,
  output [31:0] sp,
  output [31:0] t0,
  output [31:0] t1,
  output [31:0] t2,
  output [31:0] s0,
  output [31:0] s1,
  output [31:0] a0,
  output [31:0] Read_Data_1,
  output [31:0] Read_Data_2
);

  wire x1, x2, x3, x4, x5, x6, x7, x8, x9, x10, x11, x12, x13, x14, x15, x16, x17, x18, x19, x20, x21, x22,
       x23, x24, x25, x26, x27, x28, x29, x30, x31;
  wire [31:0] a1, a2, a3, a4, a5, a6, a7, gp, s2, s3, s4, s5, s6, s7, s8, s9, s10, s11, t3, t4, t5, t6, tp;

  Demultiplexer #(.enable("false"), .select(5)) demultiplexer_1 (
    .out1(x1), .out2(x2), .out3(x3), .out4(x4), .out5(x5), .out6(x6), .out7(x7), .out8(x8), .out9(x9),
    .out10(x10), .out11(x11), .out12(x12), .out13(x13), .out14(x14), .out15(x15), .out16(x16), .out17(x17),
    .out18(x18), .out19(x19), .out20(x20), .out21(x21), .out22(x22), .out23(x23), .out24(x24), .out25(x25),
    .out26(x26), .out27(x27), .out28(x28), .out29(x29), .out30(x30), .out31(x31), .in(RegWEn), .sel(rd));  // open: out0
  Multiplexer #(.enable("false"), .select(5), .width(32)) multiplexer_1 (
    .in0({32{1'b0}}), .in1(ra), .in2(sp), .in3(gp), .in4(tp), .in5(t0), .in6(t1), .in7(t2), .in8(s0),
    .in9(s1), .in10(a0), .in11(a1), .in12(a2), .in13(a3), .in14(a4), .in15(a5), .in16(a6), .in17(a7),
    .in18(s2), .in19(s3), .in20(s4), .in21(s5), .in22(s6), .in23(s7), .in24(s8), .in25(s9), .in26(s10),
    .in27(s11), .in28(t3), .in29(t4), .in30(t5), .in31(t6), .out(Read_Data_2), .sel(rs2));
  Register #(.width(32)) register_1 (.D(Write_Data), .en(x1), .clk(clk), .Q(ra));  // open: clr
  Register #(.width(32)) register_2 (.D(Write_Data), .en(x3), .clk(clk), .Q(gp));  // open: clr
  Register #(.width(32)) register_3 (.D(Write_Data), .en(x5), .clk(clk), .Q(t0));  // open: clr
  Register #(.width(32)) register_4 (.D(Write_Data), .en(x7), .clk(clk), .Q(t2));  // open: clr
  Register #(.width(32)) register_5 (.D(Write_Data), .en(x9), .clk(clk), .Q(s1));  // open: clr
  Register #(.width(32)) register_6 (.D(Write_Data), .en(x2), .clk(clk), .Q(sp));  // open: clr
  Register #(.width(32)) register_7 (.D(Write_Data), .en(x4), .clk(clk), .Q(tp));  // open: clr
  Register #(.width(32)) register_8 (.D(Write_Data), .en(x6), .clk(clk), .Q(t1));  // open: clr
  Register #(.width(32)) register_9 (.D(Write_Data), .en(x8), .clk(clk), .Q(s0));  // open: clr
  Register #(.width(32)) register_10 (.D(Write_Data), .en(x10), .clk(clk), .Q(a0));  // open: clr
  Multiplexer #(.enable("false"), .select(5), .width(32)) multiplexer_2 (
    .in0({32{1'b0}}), .in1(ra), .in2(sp), .in3(gp), .in4(tp), .in5(t0), .in6(t1), .in7(t2), .in8(s0),
    .in9(s1), .in10(a0), .in11(a1), .in12(a2), .in13(a3), .in14(a4), .in15(a5), .in16(a6), .in17(a7),
    .in18(s2), .in19(s3), .in20(s4), .in21(s5), .in22(s6), .in23(s7), .in24(s8), .in25(s9), .in26(s10),
    .in27(s11), .in28(t3), .in29(t4), .in30(t5), .in31(t6), .out(Read_Data_1), .sel(rs1));
  Register #(.width(32)) register_11 (.D(Write_Data), .en(x11), .clk(clk), .Q(a1));  // open: clr
  Register #(.width(32)) register_12 (.D(Write_Data), .en(x13), .clk(clk), .Q(a3));  // open: clr
  Register #(.width(32)) register_13 (.D(Write_Data), .en(x15), .clk(clk), .Q(a5));  // open: clr
  Register #(.width(32)) register_14 (.D(Write_Data), .en(x17), .clk(clk), .Q(a7));  // open: clr
  Register #(.width(32)) register_15 (.D(Write_Data), .en(x19), .clk(clk), .Q(s3));  // open: clr
  Register #(.width(32)) register_16 (.D(Write_Data), .en(x12), .clk(clk), .Q(a2));  // open: clr
  Register #(.width(32)) register_17 (.D(Write_Data), .en(x14), .clk(clk), .Q(a4));  // open: clr
  Register #(.width(32)) register_18 (.D(Write_Data), .en(x16), .clk(clk), .Q(a6));  // open: clr
  Register #(.width(32)) register_19 (.D(Write_Data), .en(x18), .clk(clk), .Q(s2));  // open: clr
  Register #(.width(32)) register_20 (.D(Write_Data), .en(x20), .clk(clk), .Q(s4));  // open: clr
  Register #(.width(32)) register_21 (.D(Write_Data), .en(x25), .clk(clk), .Q(s9));  // open: clr
  Register #(.width(32)) register_22 (.D(Write_Data), .en(x27), .clk(clk), .Q(s11));  // open: clr
  Register #(.width(32)) register_23 (.D(Write_Data), .en(x29), .clk(clk), .Q(t4));  // open: clr
  Register #(.width(32)) register_24 (.D(Write_Data), .en(x21), .clk(clk), .Q(s5));  // open: clr
  Register #(.width(32)) register_25 (.D(Write_Data), .en(x23), .clk(clk), .Q(s7));  // open: clr
  Register #(.width(32)) register_26 (.D(Write_Data), .en(x22), .clk(clk), .Q(s6));  // open: clr
  Register #(.width(32)) register_27 (.D(Write_Data), .en(x24), .clk(clk), .Q(s8));  // open: clr
  Register #(.width(32)) register_28 (.D(Write_Data), .en(x26), .clk(clk), .Q(s10));  // open: clr
  Register #(.width(32)) register_29 (.D(Write_Data), .en(x28), .clk(clk), .Q(t3));  // open: clr
  Register #(.width(32)) register_30 (.D(Write_Data), .en(x30), .clk(clk), .Q(t5));  // open: clr
  Register #(.width(32)) register_31 (.D(Write_Data), .en(x31), .clk(clk), .Q(t6));  // open: clr

  // Other names for the same wires on the sheet: read_data1[31:0] = Read_Data_1; read_data2[31:0] = Read_Data_2;
  //   read_reg1[4:0] = rs1; read_reg2[4:0] = rs2; write_en = RegWEn; write_reg[4:0] = rd

  // Notes on the sheet:
  //   INPUTS to your circuit
  //   DON'T CHANGE THE LOCATIONS OF THE INPUTS AND OUTPUTS!
  //   These are DEBUG/TEST outputs from your circuit.
  //   OUTPUTS from your circuit
endmodule
